// Logisim project alu.circ as structural Verilog: 1 circuit, main circuit alu
module alu (
  input  [31:0] A,
  input  [31:0] B,
  input  [3:0] ALUSel,
  output [31:0] Result
);

  wire and_2_out, comparator_1_lt;
  wire [3:0] multiplexer_6_out, multiplexer_7_out;
  wire [27:0] multiplexer_6_out_2, multiplexer_7_out_2;
  wire [31:0] A_0, A_1, A_1_R, A_2, A_2_R, A_3, A_4_R, A_8_R, A_16_R, add0, and1, mul10, mulh14, mulhu11,
       multiplexer_2_out, multiplexer_3_out, multiplexer_9_out, multiplexer_10_out, multiplexer_12_out,
       multiplexer_14_out, or2, sll6, slt7, sra5, srl4, sub12, xor3;

  Adder #(.width(32)) adder_1 (.a(A), .b(B), .out(add0));  // open: cin, cout
  assign and1 = A & B;  // AND_Gate and_1, 32 bits wide
  assign or2 = A | B;  // OR_Gate or_1, 32 bits wide
  assign xor3 = A ^ B;  // XOR_Gate xor_1, 32 bits wide
  Multiplexer #(.enable("false"), .width(32)) multiplexer_1 (.in0(A), .in1(A_1_R), .out(A_0), .sel(B[0]));
  Multiplier #(.mode("twosComplement"), .width(32)) multiplier_1 (.a(A), .b(B), .out(mul10));  // open: cin, cout
  Multiplexer #(.enable("false"), .width(32)) multiplexer_2 (
    .in0(A), .in1({1'b0, A[31:1]}), .out(multiplexer_2_out), .sel(B[0]));
  Multiplexer #(.enable("false"), .width(32)) multiplexer_3 (
    .in0(A), .in1({A[30:0], 1'b0}), .out(multiplexer_3_out), .sel(B[0]));
  assign A_1_R = {{1{A[31]}}, A[31:1]};  // Bit_Extender bit_extender_1
  assign A_2_R = {{2{A_0[31]}}, A_0[31:2]};  // Bit_Extender bit_extender_2
  assign A_4_R = {{4{A_1[31]}}, A_1[31:4]};  // Bit_Extender bit_extender_3
  assign A_8_R = {{8{A_2[31]}}, A_2[31:8]};  // Bit_Extender bit_extender_4
  assign A_16_R = {{16{A_3[31]}}, A_3[31:16]};  // Bit_Extender bit_extender_5
  Multiplexer #(.enable("false"), .width(32)) multiplexer_4 (.in0(A_0), .in1(A_2_R), .out(A_1), .sel(B[1]));
  Multiplier #(.width(32)) multiplier_2 (.a(A), .b(B), .cout(mulhu11));  // open: out, cin
  Multiplexer #(.enable("false"), .select(4), .width(32)) multiplexer_5 (
    .in0(add0), .in1(and1), .in2(or2), .in3(xor3), .in4(srl4), .in5(sra5), .in6(sll6), .in7(slt7),
    .in10(mul10), .in11(mulhu11), .in12(sub12), .in13(B), .in14(mulh14), .out(Result), .sel(ALUSel));  // open: in8, in9, in15
  Multiplexer #(.enable("false"), .width(32)) multiplexer_6 (
    .in0(multiplexer_2_out), .in1({2'b00, multiplexer_2_out[31:2]}),
    .out({multiplexer_6_out_2, multiplexer_6_out}), .sel(B[1]));
  Multiplexer #(.enable("false"), .width(32)) multiplexer_7 (
    .in0(multiplexer_3_out), .in1({multiplexer_3_out[29:0], 2'b00}),
    .out({multiplexer_7_out, multiplexer_7_out_2}), .sel(B[1]));
  Multiplexer #(.enable("false"), .width(32)) multiplexer_8 (.in0(A_1), .in1(A_4_R), .out(A_2), .sel(B[2]));
  Multiplexer #(.enable("false"), .width(32)) multiplexer_9 (
    .in0({multiplexer_6_out_2, multiplexer_6_out}), .in1({4'b0000, multiplexer_6_out_2}),
    .out(multiplexer_9_out), .sel(B[2]));
  Multiplexer #(.enable("false"), .width(32)) multiplexer_10 (
    .in0({multiplexer_7_out, multiplexer_7_out_2}), .in1({multiplexer_7_out_2, 4'b0000}),
    .out(multiplexer_10_out), .sel(B[2]));
  Subtractor #(.width(32)) subtractor_1 (.a(A), .b(B), .out(sub12));  // open: bin, bout
  Multiplexer #(.enable("false"), .width(32)) multiplexer_11 (.in0(A_2), .in1(A_8_R), .out(A_3), .sel(B[3]));
  Comparator #(.width(32)) comparator_1 (.a(A), .b(B), .lt(comparator_1_lt));  // open: gt, eq
  assign slt7 = {{31{1'b0}}, and_2_out};  // Bit_Extender bit_extender_6
  and and_2 (and_2_out, comparator_1_lt, 1'b1);
  Multiplexer #(.enable("false"), .width(32)) multiplexer_12 (
    .in0(multiplexer_9_out), .in1({{8{1'b0}}, multiplexer_9_out[31:8]}), .out(multiplexer_12_out), .sel(B[3]));
  Multiplexer #(.enable("false"), .width(32)) multiplexer_13 (.in0(A_3), .in1(A_16_R), .out(sra5), .sel(B[4]));
  Multiplexer #(.enable("false"), .width(32)) multiplexer_14 (
    .in0(multiplexer_10_out), .in1({multiplexer_10_out[23:0], {8{1'b0}}}), .out(multiplexer_14_out),
    .sel(B[3]));
  Multiplier #(.mode("twosComplement"), .width(32)) multiplier_3 (.a(A), .b(B), .cout(mulh14));  // open: out, cin
  Multiplexer #(.enable("false"), .width(32)) multiplexer_15 (
    .in0(multiplexer_12_out), .in1({{16{1'b0}}, multiplexer_12_out[31:16]}), .out(srl4), .sel(B[4]));
  Multiplexer #(.enable("false"), .width(32)) multiplexer_16 (
    .in0(multiplexer_14_out), .in1({multiplexer_14_out[15:0], {16{1'b0}}}), .out(sll6), .sel(B[4]));

  // Other names for the same wires on the sheet: bsel13[31:0] = B

  // Notes on the sheet:
  //   INPUTS to your circuit
  //   DON'T CHANGE THE LOCATIONS OF THE INPUTS AND OUTPUTS!
  //   OUTPUT from your circuit
endmodule
