// Logisim project branch_comp.circ as structural Verilog: 1 circuit, main circuit branch_comp
module branch_comp (
  input  [31:0] rs1,
  input  [31:0] rs2,
  input  BrUn,
  output BrEq,
  output BrLt
);

  wire BrEq2, BrEqU, BrLt2, BrLtU;

  Comparator #(.width(32)) comparator_1 (.a(rs1), .b(rs2), .eq(BrEq2), .lt(BrLt2));  // open: gt
  Comparator #(.mode("unsigned"), .width(32)) comparator_2 (.a(rs1), .b(rs2), .eq(BrEqU), .lt(BrLtU));  // open: gt
  Multiplexer #(.enable("false")) multiplexer_1 (.in0(BrEq2), .in1(BrEqU), .out(BrEq), .sel(BrUn));
  Multiplexer #(.enable("false")) multiplexer_2 (.in0(BrLt2), .in1(BrLtU), .out(BrLt), .sel(BrUn));

  // Notes on the sheet:
  //   INPUTS to your circuit
  //   DON'T CHANGE THE LOCATIONS OF THE INPUTS AND OUTPUTS!
  //   OUTPUT from your circuit
endmodule
