// Logisim project control_logic.circ as structural Verilog: 1 circuit, main circuit control_logic
module control_logic (
  input  [31:0] inst,
  input  BrEq,
  input  BrLt,
  output PCSel,
  output RegWEn,
  output [2:0] ImmSel,
  output BrUn,
  output ASel,
  output BSel,
  output [3:0] ALUSel,
  output MemRW,
  output [1:0] WBSel,
  output CSRSel,
  output CSRWen
);

  wire and_1_out, comparator_1_eq, comparator_2_eq, comparator_3_eq, comparator_4_eq, comparator_5_eq,
       comparator_6_eq, comparator_7_eq, comparator_8_eq, comparator_9_eq, comparator_10_eq,
       comparator_11_eq, comparator_12_eq, comparator_13_eq, comparator_14_eq, comparator_15_eq,
       comparator_16_eq, comparator_17_eq, comparator_18_eq, comparator_19_eq, comparator_20_eq,
       comparator_21_eq, comparator_22_eq, comparator_23_eq, comparator_29_eq, comparator_30_eq,
       comparator_31_eq, comparator_32_eq, comparator_33_eq, comparator_34_eq, comparator_35_eq,
       comparator_36_eq, eleven_sel, five_sel, four_sel, fourtht_sel, not_1_out, not_2_out, one_sel,
       seven_sel, six_sel, ten_sel, thirt_sel, three_sel, twelve_sel, two_sel, zero_sel;
  wire [12:0] branchCtrl;
  wire [12:12] branchGreaterThanOrEqualCtrl, branchNotEqualCtrl;

  Comparator #(.mode("unsigned"), .width(17)) comparator_1 (
    .a(17'h33), .b({inst[31:25], inst[14:12], inst[6:0]}), .eq(comparator_1_eq));  // open: gt, lt
  Comparator #(.mode("unsigned"), .width(10)) comparator_2 (
    .a(10'h83), .b({inst[14:12], inst[6:0]}), .eq(comparator_2_eq));  // open: gt, lt
  Comparator #(.mode("unsigned"), .width(10)) comparator_3 (
    .a(10'h103), .b({inst[14:12], inst[6:0]}), .eq(comparator_3_eq));  // open: gt, lt
  Comparator #(.mode("unsigned"), .width(10)) comparator_4 (
    .a(10'h13), .b({inst[14:12], inst[6:0]}), .eq(comparator_4_eq));  // open: gt, lt
  Comparator #(.mode("unsigned"), .width(10)) comparator_5 (
    .a(10'h23), .b({inst[14:12], inst[6:0]}), .eq(comparator_5_eq));  // open: gt, lt
  Comparator #(.mode("unsigned"), .width(10)) comparator_6 (
    .a(10'h123), .b({inst[14:12], inst[6:0]}), .eq(comparator_6_eq));  // open: gt, lt
  Comparator #(.mode("unsigned"), .width(10)) comparator_7 (
    .a(10'h63), .b({inst[14:12], inst[6:0]}), .eq(comparator_7_eq));  // open: gt, lt
  Comparator #(.mode("unsigned"), .width(10)) comparator_8 (
    .a(10'he3), .b({inst[14:12], inst[6:0]}), .eq(comparator_8_eq));  // open: gt, lt
  Comparator #(.mode("unsigned"), .width(10)) comparator_9 (
    .a(10'h263), .b({inst[14:12], inst[6:0]}), .eq(comparator_9_eq));  // open: gt, lt
  Comparator #(.mode("unsigned"), .width(10)) comparator_10 (
    .a(10'h2e3), .b({inst[14:12], inst[6:0]}), .eq(comparator_10_eq));  // open: gt, lt
  Comparator #(.mode("unsigned"), .width(10)) comparator_11 (
    .a(10'h363), .b({inst[14:12], inst[6:0]}), .eq(comparator_11_eq));  // open: gt, lt
  Comparator #(.mode("unsigned"), .width(10)) comparator_12 (
    .a(10'h3e3), .b({inst[14:12], inst[6:0]}), .eq(comparator_12_eq));  // open: gt, lt
  Comparator #(.mode("unsigned"), .width(7)) comparator_13 (
    .a(7'b0010111), .b(inst[6:0]), .eq(comparator_13_eq));  // open: gt, lt
  Comparator #(.mode("unsigned"), .width(7)) comparator_14 (
    .a(7'b1101111), .b(inst[6:0]), .eq(comparator_14_eq));  // open: gt, lt
  Comparator #(.mode("unsigned"), .width(10)) comparator_15 (
    .a(10'h3), .b({inst[14:12], inst[6:0]}), .eq(comparator_15_eq));  // open: gt, lt
  Comparator #(.mode("unsigned"), .width(10)) comparator_16 (
    .a(10'ha3), .b({inst[14:12], inst[6:0]}), .eq(comparator_16_eq));  // open: gt, lt
  Comparator #(.mode("unsigned"), .width(10)) comparator_17 (
    .a(10'h67), .b({inst[14:12], inst[6:0]}), .eq(comparator_17_eq));  // open: gt, lt
  Multiplexer #(.enable("false"), .width(4)) multiplexer_1 (.in1(4'b0000), .out(ALUSel), .sel(zero_sel));  // open: in0
  Multiplexer #(.enable("false"), .width(4)) multiplexer_2 (.in1(4'b0100), .out(ALUSel), .sel(four_sel));  // open: in0
  Multiplexer #(.enable("false"), .width(4)) multiplexer_3 (.in1(4'b1010), .out(ALUSel), .sel(ten_sel));  // open: in0
  Multiplexer #(.enable("false"), .width(4)) multiplexer_4 (
    .in1(4'b1110), .out(ALUSel), .sel(fourtht_sel));  // open: in0
  or or0000 (zero_sel, comparator_1_eq, comparator_15_eq, comparator_2_eq, comparator_3_eq, comparator_4_eq, comparator_5_eq, comparator_16_eq, comparator_6_eq, comparator_7_eq, comparator_8_eq, comparator_9_eq, comparator_10_eq, comparator_11_eq, comparator_12_eq, comparator_13_eq, comparator_14_eq, comparator_17_eq);
  Comparator #(.mode("unsigned"), .width(17)) comparator_18 (
    .a(17'h2b3), .b({inst[31:25], inst[14:12], inst[6:0]}), .eq(comparator_18_eq));  // open: gt, lt
  Comparator #(.mode("unsigned"), .width(17)) comparator_19 (
    .a(17'h293), .b({inst[31:25], inst[14:12], inst[6:0]}), .eq(comparator_19_eq));  // open: gt, lt
  Comparator #(.mode("unsigned"), .width(17)) comparator_20 (
    .a(17'h82b3), .b({inst[31:25], inst[14:12], inst[6:0]}), .eq(comparator_20_eq));  // open: gt, lt
  Comparator #(.mode("unsigned"), .width(17)) comparator_21 (
    .a(17'h8293), .b({inst[31:25], inst[14:12], inst[6:0]}), .eq(comparator_21_eq));  // open: gt, lt
  Comparator #(.mode("unsigned"), .width(17)) comparator_22 (
    .a(17'hb3), .b({inst[31:25], inst[14:12], inst[6:0]}), .eq(comparator_22_eq));  // open: gt, lt
  Comparator #(.mode("unsigned"), .width(17)) comparator_23 (
    .a(17'h93), .b({inst[31:25], inst[14:12], inst[6:0]}), .eq(comparator_23_eq));  // open: gt, lt
  Comparator #(.mode("unsigned"), .width(17)) comparator_24 (
    .a(17'h433), .b({inst[31:25], inst[14:12], inst[6:0]}), .eq(ten_sel));  // open: gt, lt
  Comparator #(.mode("unsigned"), .width(17)) comparator_25 (
    .a(17'h5b3), .b({inst[31:25], inst[14:12], inst[6:0]}), .eq(eleven_sel));  // open: gt, lt
  Comparator #(.mode("unsigned"), .width(17)) comparator_26 (
    .a(17'h8033), .b({inst[31:25], inst[14:12], inst[6:0]}), .eq(twelve_sel));  // open: gt, lt
  Comparator #(.mode("unsigned"), .width(7)) comparator_27 (
    .a(7'b0110111), .b(inst[6:0]), .eq(thirt_sel));  // open: gt, lt
  Comparator #(.mode("unsigned"), .width(17)) comparator_28 (
    .a(17'h4b3), .b({inst[31:25], inst[14:12], inst[6:0]}), .eq(fourtht_sel));  // open: gt, lt
  Comparator #(.mode("unsigned"), .width(17)) comparator_29 (
    .a(17'h3b3), .b({inst[31:25], inst[14:12], inst[6:0]}), .eq(comparator_29_eq));  // open: gt, lt
  Comparator #(.mode("unsigned"), .width(10)) comparator_30 (
    .a(10'h393), .b({inst[14:12], inst[6:0]}), .eq(comparator_30_eq));  // open: gt, lt
  Comparator #(.mode("unsigned"), .width(17)) comparator_31 (
    .a(17'h333), .b({inst[31:25], inst[14:12], inst[6:0]}), .eq(comparator_31_eq));  // open: gt, lt
  Comparator #(.mode("unsigned"), .width(10)) comparator_32 (
    .a(10'h313), .b({inst[14:12], inst[6:0]}), .eq(comparator_32_eq));  // open: gt, lt
  Comparator #(.mode("unsigned"), .width(17)) comparator_33 (
    .a(17'h233), .b({inst[31:25], inst[14:12], inst[6:0]}), .eq(comparator_33_eq));  // open: gt, lt
  Comparator #(.mode("unsigned"), .width(10)) comparator_34 (
    .a(10'h213), .b({inst[14:12], inst[6:0]}), .eq(comparator_34_eq));  // open: gt, lt
  or or_1 (four_sel, comparator_18_eq, comparator_19_eq);
  or or_2 (five_sel, comparator_20_eq, comparator_21_eq);
  or or_3 (six_sel, comparator_22_eq, comparator_23_eq);
  Comparator #(.mode("unsigned"), .width(17)) comparator_35 (
    .a(17'h133), .b({inst[31:25], inst[14:12], inst[6:0]}), .eq(comparator_35_eq));  // open: gt, lt
  Comparator #(.mode("unsigned"), .width(10)) comparator_36 (
    .a(10'h113), .b({inst[14:12], inst[6:0]}), .eq(comparator_36_eq));  // open: gt, lt
  Multiplexer #(.enable("false"), .width(4)) multiplexer_5 (.in1(4'b0001), .out(ALUSel), .sel(one_sel));  // open: in0
  Multiplexer #(.enable("false"), .width(4)) multiplexer_6 (.in1(4'b0101), .out(ALUSel), .sel(five_sel));  // open: in0
  Multiplexer #(.enable("false"), .width(4)) multiplexer_7 (
    .in1(4'b1011), .out(ALUSel), .sel(eleven_sel));  // open: in0
  or or_4 (one_sel, comparator_29_eq, comparator_30_eq);
  or or_5 (two_sel, comparator_31_eq, comparator_32_eq);
  or or_6 (three_sel, comparator_33_eq, comparator_34_eq);
  or or_7 (seven_sel, comparator_35_eq, comparator_36_eq);
  Multiplexer #(.enable("false"), .width(4)) multiplexer_8 (.in1(4'b0010), .out(ALUSel), .sel(two_sel));  // open: in0
  Multiplexer #(.enable("false"), .width(4)) multiplexer_9 (.in1(4'b0110), .out(ALUSel), .sel(six_sel));  // open: in0
  Multiplexer #(.enable("false"), .width(4)) multiplexer_10 (
    .in1(4'b1100), .out(ALUSel), .sel(twelve_sel));  // open: in0
  not not_1 (not_1_out, BrEq);
  and and_1 (and_1_out, not_1_out, not_2_out);
  not not_2 (not_2_out, BrLt);
  Multiplexer #(.enable("false"), .width(4)) multiplexer_11 (
    .in1(4'b0011), .out(ALUSel), .sel(three_sel));  // open: in0
  Multiplexer #(.enable("false"), .width(4)) multiplexer_12 (
    .in1(4'b0111), .out(ALUSel), .sel(seven_sel));  // open: in0
  Multiplexer #(.enable("false"), .width(4)) multiplexer_13 (
    .in1(4'b1101), .out(ALUSel), .sel(thirt_sel));  // open: in0
  Multiplexer #(.enable("false"), .select(5), .width(13)) multiplexer_14 (
    .in0(13'h820), .in4(13'h824), .in5(13'hd64), .in8(13'h130), .in12(13'h804), .in13(13'hd24),
    .in24(branchCtrl), .in25(13'h1828), .in27(13'h1c68), .in28({{11{1'b0}}, inst[14], 1'b1}),
    .out({PCSel, RegWEn, ImmSel, BrUn, ASel, BSel, MemRW, WBSel, CSRSel, CSRWen}), .sel(inst[6:2]));  // open: in1, in2, in3, in6, in7, in9, in10, in11, in14, in15, in16, in17, in18, in19, in20, in21, in22, in23, in26, in29, in30, in31
  xor xor_1 (branchGreaterThanOrEqualCtrl[12], and_1_out, BrEq);
  not not_3 (branchNotEqualCtrl[12], BrEq);
  Multiplexer #(.enable("false"), .select(3), .width(13)) multiplexer_15 (
    .in0({BrEq, 4'b0011, inst[13], 7'b1100000}),
    .in1({branchNotEqualCtrl[12], 4'b0011, inst[13], 7'b1100000}),
    .in4({BrLt, 4'b0011, inst[13], 7'b1100000}),
    .in5({branchGreaterThanOrEqualCtrl[12], 4'b0011, inst[13], 7'b1100000}),
    .in6({BrLt, 4'b0011, inst[13], 7'b1100000}),
    .in7({branchGreaterThanOrEqualCtrl[12], 4'b0011, inst[13], 7'b1100000}), .out(branchCtrl),
    .sel(inst[14:12]));  // open: in2, in3

  // Other names for the same wires on the sheet: alu_eater[16:0] = {inst[31:25], inst[14:12], inst[6:0]};
  //   nine = inst[30]; alu_eater_diet[9:0] = {inst[14:12], inst[6:0]}; opcode[6:0] = inst[6:0];
  //   actual_op[4:0] = inst[6:2]; opcode5[4:0] = inst[6:2]; funct3[2:0] = inst[14:12];
  //   branchEqualCtrl (some bits) = {BrEq, inst[13]}; branchGreaterThanOrEqualCtrl[7] = inst[13];
  //   branchLessThanCtrl (some bits) = {BrLt, inst[13]}; branchNotEqualCtrl[7] = inst[13]; funct3MidBit = inst[13];
  //   csrCtrl[1] = inst[14]; funct3FirstBit = inst[14]

  // Notes on the sheet:
  //   INPUTS to your circuit
  //   DON'T CHANGE THE LOCATIONS OF THE INPUTS AND OUTPUTS!
  //   OUTPUT from your circuit
endmodule
