// Logisim project cpu.circ as structural Verilog: 1 circuit, main circuit cpu
module cpu (
  input  clk,
  input  [31:0] INSTRUCTION,
  input  [31:0] READ_DATA,
  output [31:0] WRITE_ADDRESS,
  output [31:0] PROGRAM_COUNTER,
  output [31:0] ra,
  output [31:0] sp,
  output [31:0] t0,
  output [31:0] t1,
  output [31:0] t2,
  output [31:0] s0,
  output [31:0] s1,
  output [31:0] a0,
  output [31:0] tohost,
  output [3:0] WRITE_ENABLE,
  output [31:0] WRITE_DATA
);

  wire ASel, BrEq, BrLt, BrUn, BSel, CSRSel, CSRWen, MemRW, PCSel, RegWEn;
  wire [1:0] WBSel;
  wire [2:0] ImmSel;
  wire [3:0] ALUSel;
  wire [11:0] CSRaddr;
  wire [19:0] pipers;
  wire [31:0] adder_1_out, adder_2_out, bit_extender_1_out, bit_extender_2_out, bit_extender_3_out,
       imm_gen_1_imm, multiplexer_1_out, multiplexer_2_out, multiplexer_3_out, multiplexer_4_out,
       multiplexer_5_out, multiplexer_7_out, multiplexer_8_out, pcPL, regfile_1_read_data_1;

  Adder #(.width(32)) adder_1 (.a(PROGRAM_COUNTER), .b(32'h4), .out(adder_1_out));  // open: cin, cout
  Multiplexer #(.enable("false"), .width(32)) multiplexer_1 (
    .in0(INSTRUCTION), .in1(32'h13), .out(multiplexer_1_out), .sel(PCSel));
  Multiplexer #(.enable("false"), .width(32)) multiplexer_2 (
    .in0(adder_1_out), .in1(WRITE_ADDRESS), .out(multiplexer_2_out), .sel(PCSel));
  Register #(.width(32)) register_1 (.D(multiplexer_1_out), .en(1'b1), .clk(clk), .Q({CSRaddr, pipers}));  // open: clr
  Register #(.width(32)) PC (.D(multiplexer_2_out), .clk(clk), .Q(PROGRAM_COUNTER));  // open: en, clr
  imm_gen imm_gen_1 (.inst({CSRaddr, pipers}), .ImmSel(ImmSel), .imm(imm_gen_1_imm));
  control_logic control_logic_1 (
    .CSRWen(CSRWen), .PCSel(PCSel), .RegWEn(RegWEn), .ImmSel(ImmSel), .BrUn(BrUn), .ASel(ASel), .BSel(BSel),
    .ALUSel(ALUSel), .MemRW(MemRW), .WBSel(WBSel), .CSRSel(CSRSel), .inst({CSRaddr, pipers}), .BrEq(BrEq),
    .BrLt(BrLt));
  regfile regfile_1 (
    .rs1(pipers[19:15]), .rs2(CSRaddr[4:0]), .rd(pipers[11:7]), .Write_Data(multiplexer_8_out),
    .RegWEn(RegWEn), .clk(clk), .ra(ra), .sp(sp), .t0(t0), .t1(t1), .t2(t2), .s0(s0), .s1(s1), .a0(a0),
    .Read_Data_1(regfile_1_read_data_1), .Read_Data_2(WRITE_DATA));
  assign bit_extender_1_out = {{27{1'b0}}, pipers[19:15]};  // Bit_Extender bit_extender_1
  Multiplexer #(.enable("false"), .width(32)) multiplexer_3 (
    .in0(regfile_1_read_data_1), .in1(bit_extender_1_out), .out(multiplexer_3_out), .sel(CSRSel));
  branch_comp branch_comp_1 (.rs1(regfile_1_read_data_1), .rs2(WRITE_DATA), .BrUn(BrUn), .BrEq(BrEq), .BrLt(BrLt));
  csr csr_1 (.CSR_address(CSRaddr), .CSR_din(multiplexer_3_out), .CSR_WE(CSRWen), .clk(clk), .tohost(tohost));
  Multiplexer #(.enable("false"), .width(32)) multiplexer_4 (
    .in0(regfile_1_read_data_1), .in1(pcPL), .out(multiplexer_4_out), .sel(ASel));
  Multiplexer #(.enable("false"), .width(32)) multiplexer_5 (
    .in0(WRITE_DATA), .in1(imm_gen_1_imm), .out(multiplexer_5_out), .sel(BSel));
  alu alu_1 (.Result(WRITE_ADDRESS), .A(multiplexer_4_out), .B(multiplexer_5_out), .ALUSel(ALUSel));
  Multiplexer #(.enable("false"), .width(4)) multiplexer_6 (
    .in0(4'b0000), .in1({{2{pipers[13]}}, pipers[12], 1'b1}), .out(WRITE_ENABLE), .sel(MemRW));
  Register #(.width(32)) register_2 (.D(PROGRAM_COUNTER), .clk(clk), .Q(pcPL));  // open: en, clr
  assign bit_extender_2_out = {{24{READ_DATA[7]}}, READ_DATA[7:0]};  // Bit_Extender bit_extender_2
  assign bit_extender_3_out = {{16{READ_DATA[15]}}, READ_DATA[15:0]};  // Bit_Extender bit_extender_3
  Multiplexer #(.enable("false"), .select(2), .width(32)) multiplexer_7 (
    .in0(bit_extender_2_out), .in1(bit_extender_3_out), .in2(READ_DATA), .out(multiplexer_7_out),
    .sel(pipers[13:12]));  // open: in3
  Adder #(.width(32)) adder_2 (.a(pcPL), .b(32'h4), .out(adder_2_out));  // open: cin, cout
  Multiplexer #(.enable("false"), .select(2), .width(32)) multiplexer_8 (
    .in0(multiplexer_7_out), .in1(WRITE_ADDRESS), .in2(adder_2_out), .out(multiplexer_8_out), .sel(WBSel));  // open: in3

  // Other names for the same wires on the sheet: pipers[31:20] = CSRaddr

  // Notes on the sheet:
  //   Output to IMEM
  //   IMEM (do **NOT** move this)
  //   Inputs from IMEM
  //   It is OK to move the PC, RegFile, ALU, MEM, Branch Comp, Imm Gen, and Control Logic to wherever is most convenient for you when constructing your CPU, and to delete this text
  //   Inputs/Outputs for testing. Do **NOT** move these.
  //   Outputs To DMEM
  //   DMEM (do **NOT** move this)
  //   Inputs From DMEM
endmodule
