// Logisim project imm_gen.circ as structural Verilog: 1 circuit, main circuit imm_gen
module imm_gen (
  input  [31:0] inst,
  input  [2:0] ImmSel,
  output [31:0] imm
);

  wire [31:0] bit_extender_2_out, bType, iType, sType;

  assign sType = {{20{inst[31]}}, {inst[31:25], inst[11:7]}};  // Bit_Extender bit_extender_1
  assign bit_extender_2_out = {{11{inst[31]}}, {inst[31], inst[19:12], inst[20], inst[30:21], 1'b0}};  // Bit_Extender bit_extender_2
  assign iType = {{20{inst[31]}}, inst[31:20]};  // Bit_Extender bit_extender_3
  assign bType = {{19{inst[31]}}, {inst[31], inst[7], inst[30:25], inst[11:8], 1'b0}};  // Bit_Extender bit_extender_4
  Multiplexer #(.enable("false"), .select(3), .width(32)) multiplexer_1 (
    .in0(iType), .in1(sType), .in3(bType), .in4(bit_extender_2_out), .in5({inst[31:12], {12{1'b0}}}),
    .out(imm), .sel(ImmSel));  // open: in2, in6, in7

  // Other names for the same wires on the sheet: inst24_21[3:0] = inst[24:21]; inst11_8[3:0] = inst[11:8];
  //   inst30_25[5:0] = inst[30:25]

  // Notes on the sheet:
  //   INPUTS to your circuit
  //   DON'T CHANGE THE LOCATIONS OF THE INPUTS AND OUTPUTS!
  //   OUTPUT from your circuit
endmodule
