// Logisim project regfile.circ as structural Verilog: 1 circuit, main circuit regfile
module regfile (
  input  [4:0] rs1,
  input  [4:0] rs2,
  input  [4:0] rd,
  input  [31:0] Write_Data,
  input  RegWEn,
  input  clk,
  output [31:0] ra,
  output [31:0] sp,
  output [31:0] t0,
  output [31:0] t1,
  output [31:0] t2,
  output [31:0] s0,
  output [31:0] s1,
  output [31:0] a0,
  output [31:0] Read_Data_1,
  output [31:0] Read_Data_2
);

  wire a0we, rawe, s0we, s1we, spwe, t0we, t1we, t2we, x0we, x3we, x4we, x11we, x12we, x13we, x14we, x15we,
       x16we, x17we, x18we, x19we, x20we, x21we, x22we, x23we, x24we, x25we, x26we, x27we, x28we, x29we,
       x30we, x31we;
  wire [31:0] a0w, raw, s0w, s1w, spw, t0w, t1w, t2w, x0, x0w, x3, x3w, x4, x4w, x11, x11w, x12, x12w, x13,
       x13w, x14, x14w, x15, x15w, x16, x16w, x17, x17w, x18, x18w, x19, x19w, x20, x20w, x21, x21w, x22,
       x22w, x23, x23w, x24, x24w, x25, x25w, x26, x26w, x27, x27w, x28, x28w, x29, x29w, x30, x30w, x31,
       x31w;

  Register #(.width(32)) u_x0 (.D(x0w), .en(1'b0), .clk(clk), .Q(x0), .clr(1'b1));
  Register #(.width(32)) u_x3 (.D(x3w), .en(x3we), .clk(clk), .Q(x3));  // open: clr
  Register #(.width(32)) x6 (.D(t1w), .en(t1we), .clk(clk), .Q(t1));  // open: clr
  Register #(.width(32)) x9 (.D(s1w), .en(s1we), .clk(clk), .Q(s1));  // open: clr
  Register #(.width(32)) u_x12 (.D(x12w), .en(x12we), .clk(clk), .Q(x12));  // open: clr
  Register #(.width(32)) u_x15 (.D(x15w), .en(x15we), .clk(clk), .Q(x15));  // open: clr
  Register #(.width(32)) u_x18 (.D(x18w), .en(x18we), .clk(clk), .Q(x18));  // open: clr
  Register #(.width(32)) u_x21 (.D(x21w), .en(x21we), .clk(clk), .Q(x21));  // open: clr
  Register #(.width(32)) u_x24 (.D(x24w), .en(x24we), .clk(clk), .Q(x24));  // open: clr
  Register #(.width(32)) u_x27 (.D(x27w), .en(x27we), .clk(clk), .Q(x27));  // open: clr
  Register #(.width(32)) u_x30 (.D(x30w), .en(x30we), .clk(clk), .Q(x30));  // open: clr
  Register #(.width(32)) x1 (.D(raw), .en(rawe), .clk(clk), .Q(ra));  // open: clr
  Register #(.width(32)) u_x4 (.D(x4w), .en(x4we), .clk(clk), .Q(x4));  // open: clr
  Register #(.width(32)) x7 (.D(t2w), .en(t2we), .clk(clk), .Q(t2));  // open: clr
  Register #(.width(32)) x10 (.D(a0w), .en(a0we), .clk(clk), .Q(a0));  // open: clr
  Register #(.width(32)) u_x13 (.D(x13w), .en(x13we), .clk(clk), .Q(x13));  // open: clr
  Register #(.width(32)) u_x16 (.D(x16w), .en(x16we), .clk(clk), .Q(x16));  // open: clr
  Register #(.width(32)) u_x19 (.D(x19w), .en(x19we), .clk(clk), .Q(x19));  // open: clr
  Register #(.width(32)) u_x22 (.D(x22w), .en(x22we), .clk(clk), .Q(x22));  // open: clr
  Register #(.width(32)) u_x25 (.D(x25w), .en(x25we), .clk(clk), .Q(x25));  // open: clr
  Register #(.width(32)) u_x28 (.D(x28w), .en(x28we), .clk(clk), .Q(x28));  // open: clr
  Register #(.width(32)) u_x31 (.D(x31w), .en(x31we), .clk(clk), .Q(x31));  // open: clr
  Multiplexer #(.enable("false"), .select(5), .width(32)) multiplexer_1 (
    .in0(x0), .in1(ra), .in2(sp), .in3(x3), .in4(x4), .in5(t0), .in6(t1), .in7(t2), .in8(s0), .in9(s1),
    .in10(a0), .in11(x11), .in12(x12), .in13(x13), .in14(x14), .in15(x15), .in16(x16), .in17(x17),
    .in18(x18), .in19(x19), .in20(x20), .in21(x21), .in22(x22), .in23(x23), .in24(x24), .in25(x25),
    .in26(x26), .in27(x27), .in28(x28), .in29(x29), .in30(x30), .in31(x31), .out(Read_Data_2), .sel(rs2));
  Multiplexer #(.enable("false"), .select(5), .width(32)) multiplexer_2 (
    .in0(x0), .in1(ra), .in2(sp), .in3(x3), .in4(x4), .in5(t0), .in6(t1), .in7(t2), .in8(s0), .in9(s1),
    .in10(a0), .in11(x11), .in12(x12), .in13(x13), .in14(x14), .in15(x15), .in16(x16), .in17(x17),
    .in18(x18), .in19(x19), .in20(x20), .in21(x21), .in22(x22), .in23(x23), .in24(x24), .in25(x25),
    .in26(x26), .in27(x27), .in28(x28), .in29(x29), .in30(x30), .in31(x31), .out(Read_Data_1), .sel(rs1));
  Register #(.width(32)) x2 (.D(spw), .en(spwe), .clk(clk), .Q(sp));  // open: clr
  Register #(.width(32)) x5 (.D(t0w), .en(t0we), .clk(clk), .Q(t0));  // open: clr
  Register #(.width(32)) x8 (.D(s0w), .en(s0we), .clk(clk), .Q(s0));  // open: clr
  Register #(.width(32)) u_x11 (.D(x11w), .en(x11we), .clk(clk), .Q(x11));  // open: clr
  Register #(.width(32)) u_x14 (.D(x14w), .en(x14we), .clk(clk), .Q(x14));  // open: clr
  Register #(.width(32)) u_x17 (.D(x17w), .en(x17we), .clk(clk), .Q(x17));  // open: clr
  Register #(.width(32)) u_x20 (.D(x20w), .en(x20we), .clk(clk), .Q(x20));  // open: clr
  Register #(.width(32)) u_x23 (.D(x23w), .en(x23we), .clk(clk), .Q(x23));  // open: clr
  Register #(.width(32)) u_x26 (.D(x26w), .en(x26we), .clk(clk), .Q(x26));  // open: clr
  Register #(.width(32)) u_x29 (.D(x29w), .en(x29we), .clk(clk), .Q(x29));  // open: clr
  Demultiplexer #(.enable("false"), .select(5)) demultiplexer_1 (
    .out0(x0we), .out1(rawe), .out2(spwe), .out3(x3we), .out4(x4we), .out5(t0we), .out6(t1we), .out7(t2we),
    .out8(s0we), .out9(s1we), .out10(a0we), .out11(x11we), .out12(x12we), .out13(x13we), .out14(x14we),
    .out15(x15we), .out16(x16we), .out17(x17we), .out18(x18we), .out19(x19we), .out20(x20we), .out21(x21we),
    .out22(x22we), .out23(x23we), .out24(x24we), .out25(x25we), .out26(x26we), .out27(x27we), .out28(x28we),
    .out29(x29we), .out30(x30we), .out31(x31we), .in(RegWEn), .sel(rd));
  Demultiplexer #(.enable("false"), .select(5), .width(32)) demultiplexer_2 (
    .out0(x0w), .out1(raw), .out2(spw), .out3(x3w), .out4(x4w), .out5(t0w), .out6(t1w), .out7(t2w),
    .out8(s0w), .out9(s1w), .out10(a0w), .out11(x11w), .out12(x12w), .out13(x13w), .out14(x14w),
    .out15(x15w), .out16(x16w), .out17(x17w), .out18(x18w), .out19(x19w), .out20(x20w), .out21(x21w),
    .out22(x22w), .out23(x23w), .out24(x24w), .out25(x25w), .out26(x26w), .out27(x27w), .out28(x28w),
    .out29(x29w), .out30(x30w), .out31(x31w), .in(Write_Data), .sel(rd));

  // Other names for the same wires on the sheet: read_data1[31:0] = Read_Data_1; read_data2[31:0] = Read_Data_2;
  //   read_reg1[4:0] = rs1; read_reg2[4:0] = rs2; write_en = RegWEn; write_reg[4:0] = rd

  // Notes on the sheet:
  //   INPUTS to your circuit
  //   DON'T CHANGE THE LOCATIONS OF THE INPUTS AND OUTPUTS!
  //   These are DEBUG/TEST outputs from your circuit.
  //   OUTPUTS from your circuit
endmodule
